// Logisim project Dekoder.circ as structural Verilog: 1 circuit, main circuit Dekoder
module Dekoder (
  input  x1,
  input  x2,
  input  x3,
  output D0,
  output D1,
  output D2,
  output D3,
  output D4,
  output D5,
  output D6,
  output D7
);

  Decoder #(.select(3)) decoder_1 (
    .out0(D0), .out1(D1), .out2(D2), .out3(D3), .out4(D4), .out5(D5), .out6(D6), .out7(D7),
    .sel({x1, x2, x3}), .en(1'b1));
endmodule
